# Fritzing sketch wiringdiagram (saved by Fritzing 0.9.10b)
breadboards: 1

parts:
  M2 = Dagu DGServo 9g (Top view) [part_number=RS001B]
  U1 = ESP32-38PinWide [part_number=ESP32-38PinWide]
  M5 = Dagu DGServo 9g (Top view) [part_number=RS001B]
  M6 = Dagu DGServo 9g (Top view) [part_number=RS001B]
  M7 = Dagu DGServo 9g (Top view) [part_number=RS001B]
  VCC1 = Battery block 9V  # not connected

nets:
  GND: M2.gnd, U1.GPIO11, M5.gnd, M6.gnd, M7.gnd
  VCC: M2.vcc, U1.3.3, M5.vcc, M6.vcc, M7.vcc
  N1: M2.pulse, U1.GPIO16
  N2: U1.GPIO2, M7.pulse
  N3: U1.GPIO0, M6.pulse
  N4: U1.GPIO4, M5.pulse

notes:
  Servos for leg movement
  Red: VCC
  Brown: GND
  Orange: PWM
  ESP32-D0WDQ6 Development Board
  Black: GND
  9V battery for power

custom parts:
  ESP32-38PinWide: Generic 38-Pin ESP32 with wide format (only access to one side of pins on a breadboard) based on Stephen Lilley's HiLetgo ESP-WROOM-32 ESP32 ESP-32S Development Board.
