# Fritzing sketch wiringdiagram (saved by Fritzing 0.9.10b)
perfboards: 1

parts:
  M2 = Dagu DGServo 9g (Top view) [part_number=RS001B]
  U1 = ESP32-38PinWide [part_number=ESP32-38PinWide]
  M5 = Dagu DGServo 9g (Top view) [part_number=RS001B]
  M6 = Dagu DGServo 9g (Top view) [part_number=RS001B]
  M7 = Dagu DGServo 9g (Top view) [part_number=RS001B]
  VCC1 = Battery block 9V
  U2 = Voltage Regulator - 5V [package="TO220 [THT]"]
  Grove1 = Grove OLED 128x96

nets:
  GND: M2.gnd, M5.gnd
  N1: M2.pulse, U1.GPIO18
  N2: U1.GPIO7, Grove1.SDA
  N3: U1.GPIO2, Grove1.SCL
  N4: U1.GPIO16, M7.pulse
  N5: U1.GPIO17, M6.pulse
  N6: U1.GPIO5, M5.pulse
  N7: VCC1.-, U2.GND
  N8: VCC1.+, U2.input_voltage

notes:
  Servos for leg movement
  ESP32-D0WDQ6 Development Board
  9V battery for power
  Voltage regulator (5V out)
  OLED display for face
  ESP powered via split micro-USB cable

custom parts:
  ESP32-38PinWide: Generic 38-Pin ESP32 with wide format (only access to one side of pins on a breadboard) based on Stephen Lilley's HiLetgo ESP-WROOM-32 ESP32 ESP-32S Development Board.
